// Logisim project FSM_fechadura_sequencial.circ as structural Verilog: 5 circuits, main circuit encoder
module main (
  input  [3:0] in_1,
  input  [3:0] in_2,
  input  [3:0] in_3,
  input  [3:0] in_4
);

  wire and_1_out, button_1_out, button_2_out, button_3_out, button_4_out, button_5_out, button_6_out,
       button_7_out, button_8_out, button_9_out, button_10_out, button_11_out, clock_1_out, memory_1_q0,
       memory_1_q1, memory_1_q2, memory_1_q3, nand_1_out, next_state_function_1_d, next_state_function_1_en,
       next_state_function_1_ld, or_1_out, output_function_1_u, s0, s1;
  wire [3:0] encoder_1_b0, multiplexer_1_out, xnor_1_out;

  Button button_1 (.out(button_1_out));
  Button button_2 (.out(button_2_out));
  Button button_3 (.out(button_3_out));
  Button button_4 (.out(button_4_out));
  Button button_5 (.out(button_5_out));
  Button button_6 (.out(button_6_out));
  Button button_7 (.out(button_7_out));
  Button button_8 (.out(button_8_out));
  Button button_9 (.out(button_9_out));
  Button button_10 (.out(button_10_out));
  Multiplexer #(.select(2), .width(4)) multiplexer_1 (
    .in0(in_1), .in1(in_2), .in2(in_3), .in3(in_4), .out(multiplexer_1_out), .sel({s1, s0}));
  Button button_11 (.out(button_11_out));
  next_state_function next_state_function_1 (
    .Q0(memory_1_q0), .Q1(memory_1_q1), .Q2(memory_1_q2), .Q3(memory_1_q3), .c(and_1_out), .p(or_1_out),
    .reset(button_11_out), .En(next_state_function_1_en), .Ld(next_state_function_1_ld),
    .d(next_state_function_1_d));
  Clock clock_1 (.out(clock_1_out));
  encoder encoder_1 (
    .d9(button_4_out), .d8(button_5_out), .d7(button_1_out), .d6(button_6_out), .d5(button_7_out),
    .d4(button_2_out), .d3(button_8_out), .d2(button_9_out), .d1(button_3_out), .d0(button_10_out),
    .b3(encoder_1_b0[3]), .b2(encoder_1_b0[2]), .b1(encoder_1_b0[1]), .b0(encoder_1_b0[0]));
  assign xnor_1_out = ~(multiplexer_1_out ^ encoder_1_b0);  // XNOR_Gate xnor_1, 4 bits wide
  memory memory_1 (
    .En(next_state_function_1_en), .Ld(next_state_function_1_ld), .d0(next_state_function_1_d),
    .d1(next_state_function_1_d), .d2(next_state_function_1_d), .d3(next_state_function_1_d),
    .CLK(clock_1_out), .Q0(memory_1_q0), .Q1(memory_1_q1), .Q2(memory_1_q2), .Q3(memory_1_q3));
  and and_1 (and_1_out, xnor_1_out[0], xnor_1_out[1], xnor_1_out[2], xnor_1_out[3]);
  nand nand_1 (nand_1_out, encoder_1_b0[3], encoder_1_b0[2], encoder_1_b0[1], encoder_1_b0[0]);
  or or_1 (or_1_out, nand_1_out, button_11_out);
  output_function output_function_1 (
    .Q0(memory_1_q0), .Q1(memory_1_q1), .Q2(memory_1_q2), .Q3(memory_1_q3), .s1(s1), .s0(s0),
    .u(output_function_1_u));
  LED led_1 (.in(output_function_1_u));

  // Notes on the sheet:
  //   d0
  //   d1
  //   d2
  //   d3
  //   7
  //   4
  //   1
  //   Senha cadastrada: 4952
  //   Input
  //   8
  //   9
  //   5
  //   6
  //   2
  //   3
  //   0
  //   reset
endmodule

module encoder (
  input  d9,
  input  d8,
  input  d7,
  input  d6,
  input  d5,
  input  d4,
  input  d3,
  input  d2,
  input  d1,
  input  d0,
  output b3,
  output b2,
  output b1,
  output b0
);

  wire nand_1_out, nand_2_out, nand_3_out, nand_4_out, nand_5_out, nand_6_out, nand_7_out, nand_8_out,
       nand_9_out, nand_10_out, nand_11_out, nand_12_out, nand_13_out, nand_14_out;

  nand nand_1 (nand_1_out, 1'b1, d9);
  nand nand_2 (nand_2_out, 1'b1, d8);
  nand nand_3 (nand_3_out, 1'b1, d7);
  nand nand_4 (nand_4_out, 1'b1, d6);
  nand nand_5 (nand_5_out, 1'b1, d5);
  nand nand_6 (nand_6_out, 1'b1, d4);
  nand nand_7 (nand_7_out, 1'b1, d3);
  nand nand_8 (nand_8_out, 1'b1, d2);
  nand nand_9 (nand_9_out, 1'b1, d1);
  nand nand_10 (nand_10_out, 1'b1, d0);
  nand nand_11 (nand_11_out, nand_3_out, nand_4_out, nand_5_out, nand_6_out, nand_7_out, nand_8_out, nand_9_out, nand_10_out);
  nand nand_12 (nand_12_out, nand_1_out, nand_2_out, nand_7_out, nand_8_out, nand_9_out, nand_10_out);
  nand nand_13 (nand_13_out, nand_1_out, nand_2_out, nand_5_out, nand_6_out, nand_9_out, nand_10_out);
  nand nand_14 (nand_14_out, nand_2_out, nand_4_out, nand_6_out, nand_8_out, nand_10_out);
  nand nand_15 (b3, nand_11_out, nand_11_out);
  nand nand_16 (b2, nand_12_out, nand_12_out);
  nand nand_17 (b1, nand_13_out, nand_13_out);
  nand nand_18 (b0, nand_14_out, nand_14_out);
endmodule

module next_state_function (
  input  Q0,
  input  Q1,
  input  Q2,
  input  Q3,
  input  c,
  input  p,
  input  reset,
  output En,
  output Ld,
  output d
);

  wire nand_1_out, nand_2_out, nand_3_out, nand_4_out, nand_5_out, nand_6_out, nand_7_out, nand_8_out,
       nand_9_out, not_1_out, not_2_out, not_3_out, not_4_out, not_5_out, not_6_out, not_7_out;

  not not_1 (not_1_out, Q0);
  not not_2 (not_2_out, Q1);
  not not_3 (not_3_out, Q2);
  not not_4 (not_4_out, Q3);
  not not_5 (not_5_out, c);
  not not_6 (not_6_out, p);
  not not_7 (not_7_out, reset);
  nand nand_1 (nand_1_out, Q3, not_3_out, Q1);
  nand nand_2 (nand_2_out, Q3, Q2, not_1_out);
  nand nand_3 (nand_3_out, Q3, Q2, not_2_out);
  nand nand_4 (nand_4_out, not_4_out, Q0, not_6_out);
  nand nand_5 (nand_5_out, not_4_out, not_1_out, p);
  nand nand_6 (nand_6_out, Q3, not_3_out, Q0, not_5_out);
  nand nand_7 (nand_7_out, Q3, not_3_out, Q0, p);
  nand nand_8 (nand_8_out, Q3, not_1_out, not_6_out, c);
  nand nand_9 (nand_9_out, p, not_5_out);
  nand nand_10 (Ld, not_4_out, nand_9_out, not_7_out);
  and and_1 (d, not_4_out, not_7_out);
  nand nand_11 (En, nand_1_out, nand_2_out, nand_3_out, nand_4_out, nand_5_out, nand_6_out, nand_7_out, nand_8_out, not_7_out);
endmodule

module memory (
  input  En,
  input  Ld,
  input  d0,
  input  d1,
  input  d2,
  input  d3,
  input  CLK,
  output Q0,
  output Q1,
  output Q2,
  output Q3
);

  wire d_ff_2_qn, d_ff_3_qn, d_ff_4_qn, multiplexer_1_out, multiplexer_2_out, multiplexer_3_out,
       multiplexer_4_out, n0, n1, n2, n3, nand_1_out, nand_3_out, nand_4_out, nand_5_out, nand_7_out,
       nand_8_out, nand_9_out, nand_11_out, nand_12_out;

  Multiplexer #(.select(2)) multiplexer_1 (
    .in0(Q0), .in1(Q0), .in2(n0), .in3(d0), .out(multiplexer_1_out), .sel({En, Ld}));
  Multiplexer #(.select(2)) multiplexer_2 (
    .in0(Q1), .in1(Q1), .in2(n1), .in3(d1), .out(multiplexer_2_out), .sel({En, Ld}));
  Multiplexer #(.select(2)) multiplexer_3 (
    .in0(Q2), .in1(Q2), .in2(n2), .in3(d2), .out(multiplexer_3_out), .sel({En, Ld}));
  Multiplexer #(.select(2)) multiplexer_4 (
    .in0(Q3), .in1(Q3), .in2(n3), .in3(d3), .out(multiplexer_4_out), .sel({En, Ld}));
  D_Flip_Flop d_ff_1 (.D(multiplexer_1_out), .clk(CLK), .Q(Q0), .Qn(n0));  // open: preset, reset
  D_Flip_Flop d_ff_2 (.D(multiplexer_2_out), .clk(CLK), .Q(Q1), .Qn(d_ff_2_qn));  // open: preset, reset
  D_Flip_Flop d_ff_3 (.D(multiplexer_3_out), .clk(CLK), .Q(Q2), .Qn(d_ff_3_qn));  // open: preset, reset
  D_Flip_Flop d_ff_4 (.D(multiplexer_4_out), .clk(CLK), .Q(Q3), .Qn(d_ff_4_qn));  // open: preset, reset
  nand nand_1 (nand_1_out, n0, Q1);
  nand nand_2 (n1, nand_1_out, nand_3_out);
  nand nand_3 (nand_3_out, Q0, d_ff_2_qn);
  nand nand_4 (nand_4_out, d_ff_2_qn, Q2);
  nand nand_5 (nand_5_out, n0, Q2);
  nand nand_6 (n2, nand_4_out, nand_5_out, nand_7_out);
  nand nand_7 (nand_7_out, Q0, Q1, d_ff_3_qn);
  nand nand_8 (nand_8_out, Q3, n0);
  nand nand_9 (nand_9_out, d_ff_2_qn, Q3);
  nand nand_10 (n3, nand_8_out, nand_9_out, nand_11_out, nand_12_out);
  nand nand_11 (nand_11_out, d_ff_3_qn, Q3);
  nand nand_12 (nand_12_out, Q0, Q1, Q2, d_ff_4_qn);

  // Notes on the sheet:
  //   Q0'
  //   Q1'Q0 + Q1Q0'
  //   Q2Q1' + Q2Q0' + Q2'Q1Q0
  //   Q3'Q2Q1Q0 + Q3Q2' + Q3Q1' + Q3Q0'
endmodule

module output_function (
  input  Q0,
  input  Q1,
  input  Q2,
  input  Q3,
  output s1,
  output s0,
  output u
);

  wire nand_1_out, nand_2_out, nand_3_out, nand_4_out;

  nand nand_1 (nand_1_out, 1'b1, Q0);
  nand nand_2 (nand_2_out, 1'b1, Q1);
  nand nand_3 (nand_3_out, 1'b1, Q2);
  nand nand_4 (nand_4_out, nand_1_out, nand_2_out, nand_3_out, Q3);
  nand nand_5 (u, nand_4_out, nand_4_out);

  assign s0 = Q1;
  assign s1 = Q2;
endmodule
